# Fritzing sketch pro-mini-to-rgb (saved by Fritzing 0.8.3b)
circuit board: 16.9333cm x 5.64444cm
breadboards: 1

parts:
  Part2 = Arduino Pro Mini v13
  LED1 = LED - 5mm [color="Red (633nm)" package="5 mm [THT]"]
  V1 = DC Power [voltage=5]
  LED2 = LED - 5mm [color="Blue (525nm)" package="5 mm [THT]"]
  LED3 = LED - 5mm [color="Green (570nm)" package="5 mm [THT]"]
  Q1 = TRANSISTOR_NPN [package=to-92-ammo]
  Q2 = TRANSISTOR_NPN [package=to-92-ammo]
  Q3 = TRANSISTOR_NPN [package=to-92-ammo]
  Power_plug1 = Power plug
  J1 = female pin header, 2 pins [form="♀ (female)"]  # not connected

nets:
  VCC: Part2.VCC, LED1.anode, V1.V+, LED2.anode, LED3.anode, Power_plug1.VCC
  GND: Part2.GND, V1.V-, Q1.E, Q2.E, Q3.E, Power_plug1.GND
  N1: LED1.cathode, Q2.C
  N2: LED2.cathode, Q3.C
  N3: LED3.cathode, Q1.C
